// Logisim project Fluminense.circ as structural Verilog
module ULA___8_bits (
  input  [7:0] A,
  input  [7:0] B,
  input  [2:0] Shift,
  input  [3:0] Seletor,
  output [7:0] Output,
  output out_6,
  output out_7
);

  wire [7:0] adder_1_out, and_1_out, nand_1_out, nor_1_out, not_1_out, or_1_out, shifter_1_out,
       shifter_2_out, subtractor_1_out, xor_1_out;

  assign and_1_out = A & B;  // AND_Gate and_1, 8 bits wide
  assign or_1_out = A | B;  // OR_Gate or_1, 8 bits wide
  assign not_1_out = ~A;  // NOT_Gate not_1, 8 bits wide
  assign nor_1_out = ~(A | B);  // NOR_Gate nor_1, 8 bits wide
  assign nand_1_out = ~(A & B);  // NAND_Gate nand_1, 8 bits wide
  assign xor_1_out = A ^ B;  // XOR_Gate xor_1, 8 bits wide
  Shifter shifter_1 (.in(A), .\dist (Shift), .out(shifter_1_out));
  Shifter #(.shift("lr")) shifter_2 (.in(A), .\dist (Shift), .out(shifter_2_out));
  Adder adder_1 (.a(A), .b(B), .out(adder_1_out), .cout(out_6));  // open: cin
  Subtractor subtractor_1 (.a(A), .b(B), .out(subtractor_1_out), .bout(out_7));  // open: bin
  Multiplexer #(.select(4), .width(8)) multiplexer_1 (
    .in3(and_1_out), .in4(or_1_out), .in5(not_1_out), .in6(nor_1_out), .in7(nand_1_out), .in8(xor_1_out),
    .in9(shifter_1_out), .in10(shifter_2_out), .in11(adder_1_out), .in12(subtractor_1_out), .out(Output),
    .sel(Seletor));  // open: in0, in1, in2, in13, in14, in15, en

  // Notes on the sheet:
  //   0000 AND
  //   0101 XOR
  //   0001 OR
  //   0110 Shift E
  //   Códigos do Seletor
  //   0010 NOT A
  //   0111 Shift D
  //   1000 Somador
  //   0011 NOR
  //   0100 NAND
  //   1001 Subtrator
endmodule
